# Fritzing sketch ESPLogger (saved by Fritzing 0.9.2b)
circuit board: 8.46667cm x 5.64444cm
perfboards: 1

parts:
  U1 = ESP8266 WiFi Module [part_number=ESP8266]
  R1 = Resistor [tolerance=±5% resistance=100 package=THT]
  U2 = mystery part, 3 pins [chip_label=DHT22]
  R2 = Resistor [tolerance=±5% resistance=220 package=THT]
  R3 = Resistor [tolerance=±5% resistance=220 package=THT]
  R4 = Resistor [tolerance=±5% resistance=220 package=THT]
  U3 = mystery part, 4 pins [chip_label=?]
  C1 = Electrolytic Capacitor [capacitance=1µF package="100 mil [THT, electrolytic]"]
  VCC1 = Battery

nets:
  N1: U1.GPIO_2, R3.Pin_1
  N2: U1.CH_PD, R2.Pin_1
  GND: U1.GND, U2.pin3, R3.Pin_0, U3.pin2, C1.-, VCC1.-
  N3: U1.GPIO_16, R1.Pin_0
  N4: U1.GPIO_14, U3.pin4
  N5: U1.GPIO_12, U3.pin3
  N6: U1.GPIO_13, U2.pin2, R4.Pin_0
  N7: U1.REST, R1.Pin_1
  N8: U2.pin1, R2.Pin_0, R4.Pin_1, U3.pin1, C1.+, VCC1.+
